# Fritzing sketch AtTiny-Monitor Sketch (saved by Fritzing 0.9.3b)
circuit board: 8.46667cm x 5.64444cm
breadboards: 1

parts:
  U1 = attiny85 [package=dip]
  U2 = LIPO-2000mAh [package=lipo-2000]
  Part1 = 4N25 [package=THT]
  R1 = Resistor [tolerance=±5% resistance=330 package=THT]
  J1 = JST-B3P-VH [part_number=JST-B3P-VH package=THT]
  R2 = Resistor [tolerance=±5% resistance=330k package=THT]
  R3 = Resistor [tolerance=±5% resistance=47 package=THT]
  WeMos_D1_Mini1 = WeMos D1 Mini

nets:
  N1: U1.Pin_4, U2.-, Part1.Pin_2
  N2: U1.Pin_5, R1.Pin_1
  N3: U1.Pin_8, U2.+
  N4: Part1.Pin_1, R1.Pin_0
  N5: Part1.Pin_4, J1.pin2, WeMos_D1_Mini1.G
  N6: Part1.Pin_5, J1.pin1, R2.Pin_1, WeMos_D1_Mini1.D2
  N7: J1.pin3, R3.Pin_0, WeMos_D1_Mini1.5V
  N8: R2.Pin_0, R3.Pin_1

custom parts:
  4N25: Optocoupler
