# Fritzing sketch WemosD1 (saved by Fritzing 0.9.3b)

parts:
  WeMos_D1_Mini_Protoboard_Shield1 = WeMos D1 Mini Protoboard Shield
  J2 = longpad pin header, 7 pins [form="long pad"]
  J1 = longpad pin header, 7 pins [form="long pad"]
  J3 = male pin header, 7 pins [form="♂ (male)"]

nets:
  N1: WeMos_D1_Mini_Protoboard_Shield1.5V, WeMos_D1_Mini_Protoboard_Shield1.X5-Y8, J2.pin7
  N2: WeMos_D1_Mini_Protoboard_Shield1.D0, WeMos_D1_Mini_Protoboard_Shield1.X4-Y4, J3.pin3
  N3: WeMos_D1_Mini_Protoboard_Shield1.D2, WeMos_D1_Mini_Protoboard_Shield1.X4-Y2, J3.pin1
  N4: WeMos_D1_Mini_Protoboard_Shield1.D3, WeMos_D1_Mini_Protoboard_Shield1.X4-Y3, J3.pin2
  N5: WeMos_D1_Mini_Protoboard_Shield1.D5, WeMos_D1_Mini_Protoboard_Shield1.X4-Y5, J3.pin4
  N6: WeMos_D1_Mini_Protoboard_Shield1.D6, WeMos_D1_Mini_Protoboard_Shield1.X4-Y6, J3.pin5
  N7: WeMos_D1_Mini_Protoboard_Shield1.D7, WeMos_D1_Mini_Protoboard_Shield1.X4-Y7, J3.pin6
  N8: WeMos_D1_Mini_Protoboard_Shield1.D8, WeMos_D1_Mini_Protoboard_Shield1.X4-Y8, J3.pin7
  N9: WeMos_D1_Mini_Protoboard_Shield1.G, WeMos_D1_Mini_Protoboard_Shield1.X6-Y7, J1.pin6
  N10: WeMos_D1_Mini_Protoboard_Shield1.X5-Y2, J2.pin1
  N11: WeMos_D1_Mini_Protoboard_Shield1.X5-Y3, J2.pin2
  N12: WeMos_D1_Mini_Protoboard_Shield1.X5-Y4, J2.pin3
  N13: WeMos_D1_Mini_Protoboard_Shield1.X5-Y5, J2.pin4
  N14: WeMos_D1_Mini_Protoboard_Shield1.X5-Y6, J2.pin5
  N15: WeMos_D1_Mini_Protoboard_Shield1.X5-Y7, J2.pin6
  N16: WeMos_D1_Mini_Protoboard_Shield1.X6-Y2, J1.pin1
  N17: WeMos_D1_Mini_Protoboard_Shield1.X6-Y3, J1.pin2
  N18: WeMos_D1_Mini_Protoboard_Shield1.X6-Y4, J1.pin3
  N19: WeMos_D1_Mini_Protoboard_Shield1.X6-Y5, J1.pin4
  N20: WeMos_D1_Mini_Protoboard_Shield1.X6-Y6, J1.pin5
  N21: WeMos_D1_Mini_Protoboard_Shield1.X6-Y8, J1.pin7
